// Logisim project Single_Cycle_CPU_MIPS_bsmorrison.circ as structural Verilog
module CPU (
);

  wire ALU_Src, BEQ, BNE, Clear, Clock, EX_Operation, Jump, Memory_Read, Memory_to_Register, Memory_Write,
       R_Type, Register_Destination, Register_Write, Sub, Zero;
  wire [1:0] n32_bit_alu_1_result, PC;
  wire [2:0] ALU_Control;
  wire [3:0] ALU_Op;
  wire [4:0] multiplexer_2_out;
  wire [5:0] Function, n32_bit_alu_1_result_3, Opcode;
  wire [23:0] n32_bit_alu_1_result_2;
  wire [25:6] ram_1_data;
  wire [29:0] adder_1_out, adder_2_out, multiplexer_1_out, register_1_q;
  wire [31:0] Bus_W, Extend, multiplexer_3_out, ram_2_data, register_2_bus_a, register_2_bus_b, shifter_1_out;

  Clock u_Clock (.out(Clock));
  Button u_Clear (.out(Clear));
  Multiplexer #(.select(2), .width(30)) multiplexer_1 (
    .in0(adder_1_out), .in1(adder_2_out), .in2({register_1_q[29:26], ram_1_data, Function}),
    .out(multiplexer_1_out), .sel(PC));  // open: in3, en
  ALU_Control alu_control_1 (
    .ALU_Control(ALU_Op), .Function(Function), .r_type(R_Type), .Sub(Sub), .ALU_Control_2(ALU_Control));
  Control_Unit control_unit_1 (
    .Opcode(Opcode), .Jump(Jump), .RegDest(Register_Destination), .R_Type(R_Type), .BNE(BNE), .BEQ(BEQ),
    .MemWrite(Memory_Write), .MemRead(Memory_Read), .MemToReg(Memory_to_Register), .RegWrite(Register_Write),
    .ALUSrc(ALU_Src), .ExtOp(EX_Operation), .ALUOp(ALU_Op));
  Register_part #(.width(30), .trigger("falling")) register_1 (
    .D(multiplexer_1_out), .Q(register_1_q), .clk(Clock), .clr(Clear));  // open: en
  PC_Control pc_control_1 (.Jump(Jump), .BNE(BNE), .BEQ(BEQ), .Zero(Zero), .PC(PC));
  Adder #(.width(30)) adder_1 (.a(register_1_q), .b(30'h1), .out(adder_1_out));  // open: cin, cout
  RAM #(.addrWidth(24), .dataWidth(32)) ram_1 (
    .addr(register_1_q[23:0]), .data({Opcode, ram_1_data, Function}), .ld(1'b1), .clr(Clear));  // open: sel, clk
  Sign_Extend sign_extend_1 (.Imm({ram_1_data[15:6], Function}), .ExtOp(EX_Operation), .Out(Extend));
  Multiplexer #(.width(5)) multiplexer_2 (
    .in0(ram_1_data[20:16]), .in1(ram_1_data[15:11]), .out(multiplexer_2_out), .sel(Register_Destination));  // open: en
  Adder #(.width(30)) adder_2 (.a(adder_1_out), .b(shifter_1_out[31:2]), .out(adder_2_out));  // open: cin, cout
  Shifter #(.width(32)) shifter_1 (.in(Extend), .\dist (5'b00010), .out(shifter_1_out));
  Register register_2 (
    .RW(multiplexer_2_out), .Bus_W(Bus_W), .Reg_Write(Register_Write), .Bus_A(register_2_bus_a),
    .Bus_B(register_2_bus_b), .RA(ram_1_data[25:21]), .RB(ram_1_data[20:16]));
  Multiplexer #(.width(32)) multiplexer_3 (
    .in0(register_2_bus_b), .in1(Extend), .out(multiplexer_3_out), .sel(ALU_Src));  // open: en
  _32_bit_ALU u_32_bit_alu_1 (
    .A(register_2_bus_a), .Add_Sub(Sub), .Op_Code(ALU_Control), .B(multiplexer_3_out),
    .Result({n32_bit_alu_1_result_3, n32_bit_alu_1_result_2, n32_bit_alu_1_result}));
  Zero_Flag zero_flag_1 (.Input({n32_bit_alu_1_result_3, n32_bit_alu_1_result_2, n32_bit_alu_1_result}), .Result(Zero));
  RAM #(.addrWidth(24), .dataWidth(32), .bus("separate")) ram_2 (
    .addr(n32_bit_alu_1_result_2), .din(register_2_bus_b), .data(ram_2_data), .str(Memory_Write),
    .clk(Clock), .ld(Memory_Read), .clr(Clear));  // open: sel
  Multiplexer #(.width(32)) multiplexer_4 (
    .in0({n32_bit_alu_1_result_3, n32_bit_alu_1_result_2, n32_bit_alu_1_result}), .in1(ram_2_data),
    .out(Bus_W), .sel(Memory_to_Register));  // open: en

  // Notes on the sheet:
  //   Instruction Memory
  //   RA
  //   RW
  //   Bus A
  //   Bus B
  //   Zero Flag
  //   Data Memory
endmodule

module _1_bit_ALU (
  input  A,
  input  B,
  input  Cin,
  input  Sub,
  input  [2:0] Op_Code,
  input  Less,
  output Result,
  output Set,
  output Cout
);

  wire and_1_out, nor_1_out, or_1_out, xor_1_out, xor_2_out;

  and and_1 (and_1_out, A, B);
  or or_1 (or_1_out, A, B);
  xor xor_1 (xor_1_out, A, B);
  nor nor_1 (nor_1_out, A, B);
  Adder #(.width(1)) adder_1 (.a(A), .b(xor_2_out), .out(Set), .cin(Cin), .cout(Cout));
  xor xor_2 (xor_2_out, B, Sub);
  Multiplexer #(.select(3)) multiplexer_1 (
    .in0(and_1_out), .in1(or_1_out), .in2(xor_1_out), .in3(nor_1_out), .in4(Set), .in5(Less), .out(Result),
    .sel(Op_Code));  // open: in6, in7, en
endmodule

module _32_bit_ALU (
  input  [31:0] A,
  input  Add_Sub,
  input  [2:0] Op_Code,
  input  [31:0] B,
  output [31:0] Result
);

  wire n1_bit_alu_1_cout, n1_bit_alu_2_cout, n1_bit_alu_3_cout, n1_bit_alu_4_cout, n1_bit_alu_5_cout,
       n1_bit_alu_6_cout, n1_bit_alu_7_cout, n1_bit_alu_8_cout, n1_bit_alu_9_cout, n1_bit_alu_10_cout,
       n1_bit_alu_11_cout, n1_bit_alu_12_cout, n1_bit_alu_13_cout, n1_bit_alu_14_cout, n1_bit_alu_15_cout,
       n1_bit_alu_16_cout, n1_bit_alu_17_cout, n1_bit_alu_18_cout, n1_bit_alu_19_cout, n1_bit_alu_20_cout,
       n1_bit_alu_21_cout, n1_bit_alu_22_cout, n1_bit_alu_23_cout, n1_bit_alu_24_cout, n1_bit_alu_25_cout,
       n1_bit_alu_26_cout, n1_bit_alu_27_cout, n1_bit_alu_28_cout, n1_bit_alu_29_cout, n1_bit_alu_30_cout,
       n1_bit_alu_31_cout, n1_bit_alu_32_set;

  _1_bit_ALU u_1_bit_alu_1 (
    .A(A[0]), .B(B[0]), .Cin(Add_Sub), .Sub(Add_Sub), .Less(n1_bit_alu_32_set), .Op_Code(Op_Code),
    .Result(Result[0]), .Cout(n1_bit_alu_1_cout));  // open: Set
  _1_bit_ALU u_1_bit_alu_2 (
    .A(A[1]), .B(B[1]), .Cin(n1_bit_alu_1_cout), .Sub(Add_Sub), .Less(1'b0), .Op_Code(Op_Code),
    .Result(Result[1]), .Cout(n1_bit_alu_2_cout));  // open: Set
  _1_bit_ALU u_1_bit_alu_3 (
    .A(A[2]), .B(B[2]), .Cin(n1_bit_alu_2_cout), .Sub(Add_Sub), .Less(1'b0), .Op_Code(Op_Code),
    .Result(Result[2]), .Cout(n1_bit_alu_3_cout));  // open: Set
  _1_bit_ALU u_1_bit_alu_4 (
    .A(A[3]), .B(B[3]), .Cin(n1_bit_alu_3_cout), .Sub(Add_Sub), .Less(1'b0), .Op_Code(Op_Code),
    .Result(Result[3]), .Cout(n1_bit_alu_4_cout));  // open: Set
  _1_bit_ALU u_1_bit_alu_5 (
    .A(A[4]), .B(B[4]), .Cin(n1_bit_alu_4_cout), .Sub(Add_Sub), .Less(1'b0), .Op_Code(Op_Code),
    .Result(Result[4]), .Cout(n1_bit_alu_5_cout));  // open: Set
  _1_bit_ALU u_1_bit_alu_6 (
    .A(A[5]), .B(B[5]), .Cin(n1_bit_alu_5_cout), .Sub(Add_Sub), .Less(1'b0), .Op_Code(Op_Code),
    .Result(Result[5]), .Cout(n1_bit_alu_6_cout));  // open: Set
  _1_bit_ALU u_1_bit_alu_7 (
    .A(A[6]), .B(B[6]), .Cin(n1_bit_alu_6_cout), .Sub(Add_Sub), .Less(1'b0), .Op_Code(Op_Code),
    .Result(Result[6]), .Cout(n1_bit_alu_7_cout));  // open: Set
  _1_bit_ALU u_1_bit_alu_8 (
    .A(A[7]), .B(B[7]), .Cin(n1_bit_alu_7_cout), .Sub(Add_Sub), .Less(1'b0), .Op_Code(Op_Code),
    .Result(Result[7]), .Cout(n1_bit_alu_8_cout));  // open: Set
  _1_bit_ALU u_1_bit_alu_9 (
    .A(A[8]), .B(B[8]), .Cin(n1_bit_alu_8_cout), .Sub(Add_Sub), .Less(1'b0), .Op_Code(Op_Code),
    .Result(Result[8]), .Cout(n1_bit_alu_9_cout));  // open: Set
  _1_bit_ALU u_1_bit_alu_10 (
    .A(A[9]), .B(B[9]), .Cin(n1_bit_alu_9_cout), .Sub(Add_Sub), .Less(1'b0), .Op_Code(Op_Code),
    .Result(Result[9]), .Cout(n1_bit_alu_10_cout));  // open: Set
  _1_bit_ALU u_1_bit_alu_11 (
    .A(A[10]), .B(B[10]), .Cin(n1_bit_alu_10_cout), .Sub(Add_Sub), .Less(1'b0), .Op_Code(Op_Code),
    .Result(Result[10]), .Cout(n1_bit_alu_11_cout));  // open: Set
  _1_bit_ALU u_1_bit_alu_12 (
    .A(A[11]), .B(B[11]), .Cin(n1_bit_alu_11_cout), .Sub(Add_Sub), .Less(1'b0), .Op_Code(Op_Code),
    .Result(Result[11]), .Cout(n1_bit_alu_12_cout));  // open: Set
  _1_bit_ALU u_1_bit_alu_13 (
    .A(A[12]), .B(B[12]), .Cin(n1_bit_alu_12_cout), .Sub(Add_Sub), .Less(1'b0), .Op_Code(Op_Code),
    .Result(Result[12]), .Cout(n1_bit_alu_13_cout));  // open: Set
  _1_bit_ALU u_1_bit_alu_14 (
    .A(A[13]), .B(B[13]), .Cin(n1_bit_alu_13_cout), .Sub(Add_Sub), .Less(1'b0), .Op_Code(Op_Code),
    .Result(Result[13]), .Cout(n1_bit_alu_14_cout));  // open: Set
  _1_bit_ALU u_1_bit_alu_15 (
    .A(A[14]), .B(B[14]), .Cin(n1_bit_alu_14_cout), .Sub(Add_Sub), .Less(1'b0), .Op_Code(Op_Code),
    .Result(Result[14]), .Cout(n1_bit_alu_15_cout));  // open: Set
  _1_bit_ALU u_1_bit_alu_16 (
    .A(A[15]), .B(B[15]), .Cin(n1_bit_alu_15_cout), .Sub(Add_Sub), .Less(1'b0), .Op_Code(Op_Code),
    .Result(Result[15]), .Cout(n1_bit_alu_16_cout));  // open: Set
  _1_bit_ALU u_1_bit_alu_17 (
    .A(A[16]), .B(B[16]), .Cin(n1_bit_alu_16_cout), .Sub(Add_Sub), .Less(1'b0), .Op_Code(Op_Code),
    .Result(Result[16]), .Cout(n1_bit_alu_17_cout));  // open: Set
  _1_bit_ALU u_1_bit_alu_18 (
    .A(A[17]), .B(B[17]), .Cin(n1_bit_alu_17_cout), .Sub(Add_Sub), .Less(1'b0), .Op_Code(Op_Code),
    .Result(Result[17]), .Cout(n1_bit_alu_18_cout));  // open: Set
  _1_bit_ALU u_1_bit_alu_19 (
    .A(A[18]), .B(B[18]), .Cin(n1_bit_alu_18_cout), .Sub(Add_Sub), .Less(1'b0), .Op_Code(Op_Code),
    .Result(Result[18]), .Cout(n1_bit_alu_19_cout));  // open: Set
  _1_bit_ALU u_1_bit_alu_20 (
    .A(A[19]), .B(B[19]), .Cin(n1_bit_alu_19_cout), .Sub(Add_Sub), .Less(1'b0), .Op_Code(Op_Code),
    .Result(Result[19]), .Cout(n1_bit_alu_20_cout));  // open: Set
  _1_bit_ALU u_1_bit_alu_21 (
    .A(A[20]), .B(B[20]), .Cin(n1_bit_alu_20_cout), .Sub(Add_Sub), .Less(1'b0), .Op_Code(Op_Code),
    .Result(Result[20]), .Cout(n1_bit_alu_21_cout));  // open: Set
  _1_bit_ALU u_1_bit_alu_22 (
    .A(A[21]), .B(B[21]), .Cin(n1_bit_alu_21_cout), .Sub(Add_Sub), .Less(1'b0), .Op_Code(Op_Code),
    .Result(Result[21]), .Cout(n1_bit_alu_22_cout));  // open: Set
  _1_bit_ALU u_1_bit_alu_23 (
    .A(A[22]), .B(B[22]), .Cin(n1_bit_alu_22_cout), .Sub(Add_Sub), .Less(1'b0), .Op_Code(Op_Code),
    .Result(Result[22]), .Cout(n1_bit_alu_23_cout));  // open: Set
  _1_bit_ALU u_1_bit_alu_24 (
    .A(A[23]), .B(B[23]), .Cin(n1_bit_alu_23_cout), .Sub(Add_Sub), .Less(1'b0), .Op_Code(Op_Code),
    .Result(Result[23]), .Cout(n1_bit_alu_24_cout));  // open: Set
  _1_bit_ALU u_1_bit_alu_25 (
    .A(A[24]), .B(B[24]), .Cin(n1_bit_alu_24_cout), .Sub(Add_Sub), .Less(1'b0), .Op_Code(Op_Code),
    .Result(Result[24]), .Cout(n1_bit_alu_25_cout));  // open: Set
  _1_bit_ALU u_1_bit_alu_26 (
    .A(A[25]), .B(B[25]), .Cin(n1_bit_alu_25_cout), .Sub(Add_Sub), .Less(1'b0), .Op_Code(Op_Code),
    .Result(Result[25]), .Cout(n1_bit_alu_26_cout));  // open: Set
  _1_bit_ALU u_1_bit_alu_27 (
    .A(A[26]), .B(B[26]), .Cin(n1_bit_alu_26_cout), .Sub(Add_Sub), .Less(1'b0), .Op_Code(Op_Code),
    .Result(Result[26]), .Cout(n1_bit_alu_27_cout));  // open: Set
  _1_bit_ALU u_1_bit_alu_28 (
    .A(A[27]), .B(B[27]), .Cin(n1_bit_alu_27_cout), .Sub(Add_Sub), .Less(1'b0), .Op_Code(Op_Code),
    .Result(Result[27]), .Cout(n1_bit_alu_28_cout));  // open: Set
  _1_bit_ALU u_1_bit_alu_29 (
    .A(A[28]), .B(B[28]), .Cin(n1_bit_alu_28_cout), .Sub(Add_Sub), .Less(1'b0), .Op_Code(Op_Code),
    .Result(Result[28]), .Cout(n1_bit_alu_29_cout));  // open: Set
  _1_bit_ALU u_1_bit_alu_30 (
    .A(A[29]), .B(B[29]), .Cin(n1_bit_alu_29_cout), .Sub(Add_Sub), .Less(1'b0), .Op_Code(Op_Code),
    .Result(Result[29]), .Cout(n1_bit_alu_30_cout));  // open: Set
  _1_bit_ALU u_1_bit_alu_31 (
    .A(A[30]), .B(B[30]), .Cin(n1_bit_alu_30_cout), .Sub(Add_Sub), .Less(1'b0), .Op_Code(Op_Code),
    .Result(Result[30]), .Cout(n1_bit_alu_31_cout));  // open: Set
  _1_bit_ALU u_1_bit_alu_32 (
    .A(A[31]), .B(B[31]), .Cin(n1_bit_alu_31_cout), .Sub(Add_Sub), .Less(1'b0), .Op_Code(Op_Code),
    .Result(Result[31]), .Set(n1_bit_alu_32_set));  // open: Cout
endmodule

module ALU_Control (
  input  [3:0] ALU_Control,
  input  [5:0] Function,
  input  r_type,
  output Sub,
  output [2:0] ALU_Control_2
);

  wire ADD_out, AND_out, not_1_out, not_2_out, not_3_out, not_4_out, not_5_out, not_6_out, not_7_out,
       not_8_out, not_9_out, not_10_out, not_11_out, not_12_out, not_13_out, not_14_out, not_15_out,
       not_16_out, OR_out, SLT_out, SUB_out, XOR_out;
  wire [3:0] multiplexer_1_out;

  Multiplexer #(.width(4), .enable("false")) multiplexer_1 (
    .in0(ALU_Control), .in1(Function[3:0]), .out(multiplexer_1_out), .sel(r_type));
  not not_1 (not_1_out, multiplexer_1_out[0]);
  not not_2 (not_2_out, multiplexer_1_out[1]);
  not not_3 (not_3_out, multiplexer_1_out[2]);
  not not_4 (not_4_out, multiplexer_1_out[3]);
  not not_5 (not_5_out, multiplexer_1_out[0]);
  not not_6 (not_6_out, multiplexer_1_out[2]);
  not not_7 (not_7_out, multiplexer_1_out[3]);
  not not_8 (not_8_out, multiplexer_1_out[0]);
  not not_9 (not_9_out, multiplexer_1_out[1]);
  not not_10 (not_10_out, multiplexer_1_out[3]);
  not not_11 (not_11_out, multiplexer_1_out[1]);
  not not_12 (not_12_out, multiplexer_1_out[3]);
  not not_13 (not_13_out, multiplexer_1_out[0]);
  not not_14 (not_14_out, multiplexer_1_out[3]);
  not not_15 (not_15_out, multiplexer_1_out[0]);
  not not_16 (not_16_out, multiplexer_1_out[2]);
  and ADD (ADD_out, not_1_out, not_2_out, not_3_out, not_4_out);
  and u_SUB (SUB_out, not_5_out, multiplexer_1_out[1], not_6_out, not_7_out);
  and AND (AND_out, not_8_out, not_9_out, multiplexer_1_out[2], not_10_out);
  and OR (OR_out, multiplexer_1_out[0], not_11_out, multiplexer_1_out[2], not_12_out);
  and XOR (XOR_out, not_13_out, multiplexer_1_out[1], multiplexer_1_out[2], not_14_out);
  and SLT (SLT_out, not_15_out, multiplexer_1_out[1], not_16_out, multiplexer_1_out[3]);
  Priority_Encoder #(.select(4)) priority_encoder_1 (
    .in0(AND_out), .in1(OR_out), .in2(XOR_out), .in4(ADD_out), .in12(SUB_out), .in13(SLT_out),
    .out({Sub, ALU_Control_2}));  // open: in3, in5, in6, in7, in8, in9, in10, in11, in14, in15, gs, en_out, en_in
endmodule

module PC_Control (
  input  Jump,
  input  BNE,
  input  BEQ,
  input  Zero,
  output [1:0] PC
);

  wire and_1_out, and_2_out;

  and and_1 (and_1_out, ~Zero, BNE);  // AND_Gate
  or or_1 (PC[0], and_1_out, and_2_out);
  and and_2 (and_2_out, Zero, BEQ);

  assign PC[1] = Jump;
endmodule

module Control_Unit (
  input  [5:0] Opcode,
  output RegDest,
  output R_Type,
  output MemRead,
  output MemToReg,
  output MemWrite,
  output BEQ,
  output [3:0] ALUOp,
  output ExtOp,
  output ALUSrc,
  output RegWrite,
  output Jump,
  output BNE
);

  wire ADDI_out, ANDI_out, not_1_out, not_2_out, not_3_out, not_4_out, not_5_out, not_6_out, not_7_out,
       not_8_out, not_9_out, not_10_out, not_11_out, not_12_out, not_13_out, not_14_out, not_15_out,
       not_16_out, not_17_out, not_18_out, not_19_out, not_20_out, not_21_out, not_22_out, not_23_out,
       not_24_out, not_25_out, not_26_out, not_27_out, not_28_out, not_29_out, not_30_out, not_31_out,
       not_32_out, not_33_out, not_34_out, not_35_out, not_36_out, not_37_out, not_38_out, not_39_out,
       not_40_out, not_41_out, not_42_out, not_43_out, not_44_out, or_1_out, or_2_out, ORI_out, SLTI_out,
       XORI_out;

  not not_1 (not_1_out, Opcode[0]);
  not not_2 (not_2_out, Opcode[1]);
  not not_3 (not_3_out, Opcode[2]);
  not not_4 (not_4_out, Opcode[3]);
  not not_5 (not_5_out, Opcode[4]);
  not not_6 (not_6_out, Opcode[5]);
  not not_7 (not_7_out, Opcode[2]);
  not not_8 (not_8_out, Opcode[3]);
  not not_9 (not_9_out, Opcode[4]);
  not not_10 (not_10_out, Opcode[2]);
  not not_11 (not_11_out, Opcode[4]);
  not not_12 (not_12_out, Opcode[0]);
  not not_13 (not_13_out, Opcode[1]);
  not not_14 (not_14_out, Opcode[3]);
  not not_15 (not_15_out, Opcode[4]);
  not not_16 (not_16_out, Opcode[5]);
  not not_17 (not_17_out, Opcode[0]);
  not not_18 (not_18_out, Opcode[1]);
  not not_19 (not_19_out, Opcode[2]);
  not not_20 (not_20_out, Opcode[4]);
  not not_21 (not_21_out, Opcode[5]);
  not not_22 (not_22_out, Opcode[0]);
  not not_23 (not_23_out, Opcode[2]);
  not not_24 (not_24_out, Opcode[4]);
  not not_25 (not_25_out, Opcode[5]);
  not not_26 (not_26_out, Opcode[0]);
  not not_27 (not_27_out, Opcode[1]);
  not not_28 (not_28_out, Opcode[4]);
  not not_29 (not_29_out, Opcode[5]);
  not not_30 (not_30_out, Opcode[1]);
  not not_31 (not_31_out, Opcode[4]);
  not not_32 (not_32_out, Opcode[5]);
  not not_33 (not_33_out, Opcode[0]);
  not not_34 (not_34_out, Opcode[4]);
  not not_35 (not_35_out, Opcode[5]);
  not not_36 (not_36_out, Opcode[0]);
  not not_37 (not_37_out, Opcode[2]);
  not not_38 (not_38_out, Opcode[3]);
  not not_39 (not_39_out, Opcode[4]);
  not not_40 (not_40_out, Opcode[5]);
  not not_41 (not_41_out, Opcode[1]);
  not not_42 (not_42_out, Opcode[3]);
  not not_43 (not_43_out, Opcode[4]);
  not not_44 (not_44_out, Opcode[5]);
  and u_R_type (R_Type, not_1_out, not_2_out, not_3_out, not_4_out, not_5_out, not_6_out);
  and LW (MemRead, Opcode[0], Opcode[1], not_7_out, not_8_out, not_9_out, Opcode[5]);
  and SW (MemWrite, Opcode[0], Opcode[1], not_10_out, Opcode[3], not_11_out, Opcode[5]);
  and u_BEQ (BEQ, not_12_out, not_13_out, Opcode[2], not_14_out, not_15_out, not_16_out);
  and ADDI (ADDI_out, not_17_out, not_18_out, not_19_out, Opcode[3], not_20_out, not_21_out);
  and SLTI (SLTI_out, not_22_out, Opcode[1], not_23_out, Opcode[3], not_24_out, not_25_out);
  and ANDI (ANDI_out, not_26_out, not_27_out, Opcode[2], Opcode[3], not_28_out, not_29_out);
  and ORI (ORI_out, Opcode[0], not_30_out, Opcode[2], Opcode[3], not_31_out, not_32_out);
  and XORI (XORI_out, not_33_out, Opcode[1], Opcode[2], Opcode[3], not_34_out, not_35_out);
  and J (Jump, not_36_out, Opcode[1], not_37_out, not_38_out, not_39_out, not_40_out);
  and u_BNE (BNE, Opcode[0], not_41_out, Opcode[2], not_42_out, not_43_out, not_44_out);
  or or_1 (or_1_out, MemRead, MemWrite, ADDI_out);
  or or_2 (or_2_out, BEQ, BNE);
  nor nor_1 (ExtOp, ADDI_out, ORI_out, XORI_out);
  nor nor_2 (ALUSrc, BEQ, BNE, R_Type);
  or or_3 (RegWrite, R_Type, MemRead, ADDI_out, SLTI_out, ANDI_out, ORI_out, XORI_out);
  Priority_Encoder #(.select(4)) priority_encoder_1 (
    .in0(or_1_out), .in2(or_2_out), .in4(ANDI_out), .in5(ORI_out), .in6(XORI_out), .in10(SLTI_out),
    .out(ALUOp));  // open: in1, in3, in7, in8, in9, in11, in12, in13, in14, in15, gs, en_out, en_in

  assign MemToReg = MemRead;
  assign RegDest = R_Type;
endmodule

module Zero_Flag (
  input  [31:0] Input,
  output Result
);

  nor nor_1 (Result, Input[0], Input[1], Input[2], Input[3], Input[4], Input[5], Input[6], Input[7], Input[8], Input[9], Input[10], Input[11], Input[12], Input[13], Input[14], Input[15], Input[16], Input[17], Input[18], Input[19], Input[20], Input[21], Input[22], Input[23], Input[24], Input[25], Input[26], Input[27], Input[28], Input[29], Input[30], Input[31]);
endmodule

module Sign_Extend (
  input  [15:0] Imm,
  input  ExtOp,
  output [31:0] Out
);

  wire [31:0] bit_extender_1_out, bit_extender_2_out;

  assign bit_extender_1_out = {{16{1'b0}}, Imm};  // Bit_Extender bit_extender_1
  assign bit_extender_2_out = {{16{Imm[15]}}, Imm};  // Bit_Extender bit_extender_2
  Multiplexer #(.width(32)) multiplexer_1 (
    .in0(bit_extender_1_out), .in1(bit_extender_2_out), .out(Out), .sel(ExtOp));  // open: en
endmodule

module Register (
  input  [4:0] RW,
  input  [31:0] Bus_W,
  input  Reg_Write,
  input  [4:0] RA,
  input  [4:0] RB,
  output [31:0] Bus_A,
  output [31:0] Bus_B
);

  wire and_1_out, and_2_out, and_3_out, and_4_out, and_5_out, and_6_out, and_7_out, and_8_out, and_9_out,
       and_10_out, and_11_out, and_12_out, and_13_out, and_14_out, and_15_out, and_16_out, and_17_out,
       and_18_out, and_19_out, and_20_out, and_21_out, and_22_out, and_23_out, and_24_out, and_25_out,
       and_26_out, and_27_out, and_28_out, and_29_out, and_30_out, and_31_out, and_32_out, Clock_out;
  wire [31:0] decoder_1_out0, register_1_q, register_2_q, register_3_q, register_4_q, register_5_q,
       register_6_q, register_7_q, register_8_q, register_9_q, register_10_q, register_11_q, register_12_q,
       register_13_q, register_14_q, register_15_q, register_16_q, register_17_q, register_18_q,
       register_19_q, register_20_q, register_21_q, register_22_q, register_23_q, register_24_q,
       register_25_q, register_26_q, register_27_q, register_28_q, register_29_q, register_30_q,
       register_31_q, register_32_q;

  Clock Clock (.out(Clock_out));
  Register_part #(.width(32)) register_1 (.D(Bus_W), .en(and_1_out), .Q(register_1_q), .clk(Clock_out));  // open: clr
  Register_part #(.width(32)) register_2 (.D(Bus_W), .en(and_2_out), .Q(register_2_q), .clk(Clock_out));  // open: clr
  Decoder #(.select(5)) decoder_1 (
    .out0(decoder_1_out0[0]), .out1(decoder_1_out0[1]), .out2(decoder_1_out0[2]), .out3(decoder_1_out0[3]),
    .out4(decoder_1_out0[4]), .out5(decoder_1_out0[5]), .out6(decoder_1_out0[6]), .out7(decoder_1_out0[7]),
    .out8(decoder_1_out0[8]), .out9(decoder_1_out0[9]), .out10(decoder_1_out0[10]),
    .out11(decoder_1_out0[11]), .out12(decoder_1_out0[12]), .out13(decoder_1_out0[13]),
    .out14(decoder_1_out0[14]), .out15(decoder_1_out0[15]), .out16(decoder_1_out0[16]),
    .out17(decoder_1_out0[17]), .out18(decoder_1_out0[18]), .out19(decoder_1_out0[19]),
    .out20(decoder_1_out0[20]), .out21(decoder_1_out0[21]), .out22(decoder_1_out0[22]),
    .out23(decoder_1_out0[23]), .out24(decoder_1_out0[24]), .out25(decoder_1_out0[25]),
    .out26(decoder_1_out0[26]), .out27(decoder_1_out0[27]), .out28(decoder_1_out0[28]),
    .out29(decoder_1_out0[29]), .out30(decoder_1_out0[30]), .out31(decoder_1_out0[31]), .sel(RW));  // open: en
  and and_1 (and_1_out, Reg_Write, decoder_1_out0[15]);
  Register_part #(.width(32)) register_3 (.D(Bus_W), .en(and_4_out), .Q(register_3_q), .clk(Clock_out));  // open: clr
  Register_part #(.width(32)) register_4 (.D(Bus_W), .en(and_3_out), .Q(register_4_q), .clk(Clock_out));  // open: clr
  and and_2 (and_2_out, Reg_Write, decoder_1_out0[31]);
  Register_part #(.width(32)) register_5 (.D(Bus_W), .en(and_5_out), .Q(register_5_q), .clk(Clock_out));  // open: clr
  Register_part #(.width(32)) register_6 (.D(Bus_W), .en(and_6_out), .Q(register_6_q), .clk(Clock_out));  // open: clr
  and and_3 (and_3_out, Reg_Write, decoder_1_out0[13]);
  and and_4 (and_4_out, Reg_Write, decoder_1_out0[14]);
  Register_part #(.width(32)) register_7 (.D(Bus_W), .en(and_7_out), .Q(register_7_q), .clk(Clock_out));  // open: clr
  Register_part #(.width(32)) register_8 (.D(Bus_W), .en(and_8_out), .Q(register_8_q), .clk(Clock_out));  // open: clr
  and and_5 (and_5_out, Reg_Write, decoder_1_out0[30]);
  and and_6 (and_6_out, Reg_Write, decoder_1_out0[29]);
  Register_part #(.width(32)) register_9 (.D(Bus_W), .en(and_9_out), .Q(register_9_q), .clk(Clock_out));  // open: clr
  and and_7 (and_7_out, Reg_Write, decoder_1_out0[11]);
  and and_8 (and_8_out, Reg_Write, decoder_1_out0[12]);
  Register_part #(.width(32)) register_10 (
    .D(Bus_W), .en(and_11_out), .Q(register_10_q), .clk(Clock_out));  // open: clr
  and and_9 (and_9_out, Reg_Write, decoder_1_out0[28]);
  and and_10 (and_10_out, Reg_Write, decoder_1_out0[27]);
  Register_part #(.width(32)) register_11 (
    .D(Bus_W), .en(and_14_out), .Q(register_11_q), .clk(Clock_out));  // open: clr
  Register_part #(.width(32)) register_12 (
    .D(Bus_W), .en(and_10_out), .Q(register_12_q), .clk(Clock_out));  // open: clr
  and and_11 (and_11_out, Reg_Write, decoder_1_out0[10]);
  and and_12 (and_12_out, Reg_Write, decoder_1_out0[9]);
  Register_part #(.width(32)) register_13 (
    .D(Bus_W), .en(and_12_out), .Q(register_13_q), .clk(Clock_out));  // open: clr
  Register_part #(.width(32)) register_14 (
    .D(Bus_W), .en(and_15_out), .Q(register_14_q), .clk(Clock_out));  // open: clr
  and and_13 (and_13_out, Reg_Write, decoder_1_out0[25]);
  and and_14 (and_14_out, Reg_Write, decoder_1_out0[26]);
  Register_part #(.width(32)) register_15 (
    .D(Bus_W), .en(and_13_out), .Q(register_15_q), .clk(Clock_out));  // open: clr
  Register_part #(.width(32)) register_16 (
    .D(Bus_W), .en(and_17_out), .Q(register_16_q), .clk(Clock_out));  // open: clr
  and and_15 (and_15_out, Reg_Write, decoder_1_out0[8]);
  and and_16 (and_16_out, Reg_Write, decoder_1_out0[7]);
  Register_part #(.width(32)) register_17 (
    .D(Bus_W), .en(and_16_out), .Q(register_17_q), .clk(Clock_out));  // open: clr
  and and_17 (and_17_out, Reg_Write, decoder_1_out0[24]);
  and and_18 (and_18_out, Reg_Write, decoder_1_out0[23]);
  Register_part #(.width(32)) register_18 (
    .D(Bus_W), .en(and_18_out), .Q(register_18_q), .clk(Clock_out));  // open: clr
  and and_19 (and_19_out, Reg_Write, decoder_1_out0[5]);
  and and_20 (and_20_out, Reg_Write, decoder_1_out0[6]);
  Register_part #(.width(32)) register_19 (
    .D(Bus_W), .en(and_20_out), .Q(register_19_q), .clk(Clock_out));  // open: clr
  Register_part #(.width(32)) register_20 (
    .D(Bus_W), .en(and_19_out), .Q(register_20_q), .clk(Clock_out));  // open: clr
  and and_21 (and_21_out, Reg_Write, decoder_1_out0[21]);
  and and_22 (and_22_out, Reg_Write, decoder_1_out0[22]);
  Register_part #(.width(32)) register_21 (
    .D(Bus_W), .en(and_22_out), .Q(register_21_q), .clk(Clock_out));  // open: clr
  Register_part #(.width(32)) register_22 (
    .D(Bus_W), .en(and_21_out), .Q(register_22_q), .clk(Clock_out));  // open: clr
  and and_23 (and_23_out, Reg_Write, decoder_1_out0[4]);
  and and_24 (and_24_out, Reg_Write, decoder_1_out0[3]);
  Register_part #(.width(32)) register_23 (
    .D(Bus_W), .en(and_24_out), .Q(register_23_q), .clk(Clock_out));  // open: clr
  Register_part #(.width(32)) register_24 (
    .D(Bus_W), .en(and_23_out), .Q(register_24_q), .clk(Clock_out));  // open: clr
  and and_25 (and_25_out, Reg_Write, decoder_1_out0[20]);
  and and_26 (and_26_out, Reg_Write, decoder_1_out0[19]);
  Register_part #(.width(32)) register_25 (
    .D(Bus_W), .en(and_25_out), .Q(register_25_q), .clk(Clock_out));  // open: clr
  and and_27 (and_27_out, Reg_Write, decoder_1_out0[1]);
  and and_28 (and_28_out, Reg_Write, decoder_1_out0[2]);
  Register_part #(.width(32)) register_26 (
    .D(Bus_W), .en(and_28_out), .Q(register_26_q), .clk(Clock_out));  // open: clr
  and and_29 (and_29_out, Reg_Write, decoder_1_out0[17]);
  and and_30 (and_30_out, Reg_Write, decoder_1_out0[18]);
  Register_part #(.width(32)) register_27 (
    .D(Bus_W), .en(and_30_out), .Q(register_27_q), .clk(Clock_out));  // open: clr
  Register_part #(.width(32)) register_28 (
    .D(Bus_W), .en(and_26_out), .Q(register_28_q), .clk(Clock_out));  // open: clr
  and and_31 (and_31_out, Reg_Write, decoder_1_out0[0]);
  Register_part #(.width(32)) register_29 (
    .D(Bus_W), .en(and_27_out), .Q(register_29_q), .clk(Clock_out));  // open: clr
  Register_part #(.width(32)) register_30 (
    .D(Bus_W), .en(and_31_out), .Q(register_30_q), .clk(Clock_out));  // open: clr
  and and_32 (and_32_out, Reg_Write, decoder_1_out0[16]);
  Register_part #(.width(32)) register_31 (
    .D(Bus_W), .en(and_29_out), .Q(register_31_q), .clk(Clock_out));  // open: clr
  Register_part #(.width(32)) register_32 (
    .D(Bus_W), .en(and_32_out), .Q(register_32_q), .clk(Clock_out));  // open: clr
  Multiplexer #(.select(5), .width(32), .enable("false")) multiplexer_1 (
    .in0(register_30_q), .in1(register_29_q), .in2(register_26_q), .in3(register_23_q), .in4(register_24_q),
    .in5(register_20_q), .in6(register_19_q), .in7(register_17_q), .in8(register_14_q), .in9(register_13_q),
    .in10(register_10_q), .in11(register_7_q), .in12(register_8_q), .in13(register_4_q), .in14(register_3_q),
    .in15(register_1_q), .in16(register_32_q), .in17(register_31_q), .in18(register_27_q),
    .in19(register_28_q), .in20(register_25_q), .in21(register_22_q), .in22(register_21_q),
    .in23(register_18_q), .in24(register_16_q), .in25(register_15_q), .in26(register_11_q),
    .in27(register_12_q), .in28(register_9_q), .in29(register_6_q), .in30(register_5_q), .in31(register_2_q),
    .out(Bus_A), .sel(RA));
  Multiplexer #(.select(5), .width(32), .enable("false")) multiplexer_2 (
    .in0(register_30_q), .in1(register_29_q), .in2(register_26_q), .in3(register_23_q), .in4(register_24_q),
    .in5(register_20_q), .in6(register_19_q), .in7(register_17_q), .in8(register_14_q), .in9(register_13_q),
    .in10(register_10_q), .in11(register_7_q), .in12(register_8_q), .in13(register_4_q), .in14(register_3_q),
    .in15(register_1_q), .in16(register_32_q), .in17(register_31_q), .in18(register_27_q),
    .in19(register_28_q), .in20(register_25_q), .in21(register_22_q), .in22(register_21_q),
    .in23(register_18_q), .in24(register_16_q), .in25(register_15_q), .in26(register_11_q),
    .in27(register_12_q), .in28(register_9_q), .in29(register_6_q), .in30(register_5_q), .in31(register_2_q),
    .out(Bus_B), .sel(RB));
endmodule
